// Digital circuit ALU.dig as structural Verilog
module ALU (
  input  [7:0] D_IN,
  input  A_LD,
  input  A_OE,
  input  A_SEL,
  input  ALU_S0,
  input  ALU_S1,
  input  ALU_S2,
  input  nALU_OE,
  input  ALU_CIN,
  input  nSHR,
  input  SHR_IN0,
  input  nACC_OE,
  input  CLK,
  input  RST,
  output [7:0] ALU,
  output Z_FLAG,
  output C_FLAG,
  output N_FLAG,
  output V_FLAG,
  output [7:0] A_R_OUT
);

  wire _74245_1_pin19, AA0, AA1, AA2, AA3, AA4, AA5, AA6, AA7, AL0, AL1, AL2, AL3, AL4, AL5, AL6, ALCO, AO0,
       AO1, AO2, AO3, AO4, AO5, AO6, AO7, O0, O1, O2, O3;

  _74245 _74245_1 (
    .pin1(1'b0), .pin2(A_R_OUT[0]), .pin3(A_R_OUT[1]), .pin4(A_R_OUT[2]), .pin5(A_R_OUT[3]),
    .pin6(A_R_OUT[4]), .pin7(A_R_OUT[5]), .pin8(A_R_OUT[6]), .pin9(A_R_OUT[7]), .pin10(1'b0), .pin11(AO7),
    .pin12(AO6), .pin13(AO5), .pin14(AO4), .pin15(AO3), .pin16(AO2), .pin17(AO1), .pin18(AO0),
    .pin19(_74245_1_pin19), .pin20(1'b1));
  _74245 _74245_2 (
    .pin1(1'b0), .pin2(ALU[0]), .pin3(ALU[1]), .pin4(ALU[2]), .pin5(ALU[3]), .pin6(ALU[4]), .pin7(ALU[5]),
    .pin8(ALU[6]), .pin9(ALU[7]), .pin10(1'b0), .pin11(SHR_IN0), .pin12(AO7), .pin13(AO6), .pin14(AO5),
    .pin15(AO4), .pin16(AO3), .pin17(AO2), .pin18(AO1), .pin19(nSHR), .pin20(1'b1));
  and and_1 (_74245_1_pin19, nACC_OE, A_OE);
  _74257 _74257_1 (
    .pin1(A_SEL), .pin2(D_IN[0]), .pin3(AL0), .pin4(AA0), .pin5(D_IN[1]), .pin6(AL1), .pin7(AA1),
    .pin8(1'b0), .pin9(AA2), .pin10(AL2), .pin11(D_IN[2]), .pin12(AA3), .pin13(AL3), .pin14(D_IN[3]),
    .pin15(1'b0), .pin16(1'b1));
  _74173 _74173_1 (
    .pin1(1'b0), .pin2(1'b0), .pin3(AO0), .pin4(AO1), .pin5(AO2), .pin6(AO3), .pin7(CLK), .pin8(1'b0),
    .pin9(A_LD), .pin10(A_LD), .pin11(AA3), .pin12(AA2), .pin13(AA1), .pin14(AA0), .pin15(RST), .pin16(1'b1));
  _74382 _74382_1 (
    .pin1(AO1), .pin2(D_IN[1]), .pin3(AO0), .pin4(D_IN[0]), .pin5(ALU_S0), .pin6(ALU_S1), .pin7(ALU_S2),
    .pin8(AL0), .pin9(AL1), .pin10(1'b0), .pin11(AL2), .pin12(AL3), .pin14(ALCO), .pin15(ALU_CIN),
    .pin16(D_IN[3]), .pin17(AO3), .pin18(D_IN[2]), .pin19(AO2), .pin20(1'b1));  // open: pin13
  _74245 _74245_3 (
    .pin1(1'b0), .pin2(ALU[0]), .pin3(ALU[1]), .pin4(ALU[2]), .pin5(ALU[3]), .pin6(ALU[4]), .pin7(ALU[5]),
    .pin8(ALU[6]), .pin9(ALU[7]), .pin10(1'b0), .pin11(N_FLAG), .pin12(AL6), .pin13(AL5), .pin14(AL4),
    .pin15(AL3), .pin16(AL2), .pin17(AL1), .pin18(AL0), .pin19(nALU_OE), .pin20(1'b1));
  _74257 _74257_2 (
    .pin1(A_SEL), .pin2(D_IN[4]), .pin3(AL4), .pin4(AA4), .pin5(D_IN[5]), .pin6(AL5), .pin7(AA5),
    .pin8(1'b0), .pin9(AA6), .pin10(AL6), .pin11(D_IN[6]), .pin12(AA7), .pin13(N_FLAG), .pin14(D_IN[7]),
    .pin15(1'b0), .pin16(1'b1));
  _74173 _74173_2 (
    .pin1(1'b0), .pin2(1'b0), .pin3(AO4), .pin4(AO5), .pin5(AO6), .pin6(AO7), .pin7(CLK), .pin8(1'b0),
    .pin9(A_LD), .pin10(A_LD), .pin11(AA7), .pin12(AA6), .pin13(AA5), .pin14(AA4), .pin15(RST), .pin16(1'b1));
  _74382 _74382_2 (
    .pin1(AO5), .pin2(D_IN[5]), .pin3(AO4), .pin4(D_IN[4]), .pin5(ALU_S0), .pin6(ALU_S1), .pin7(ALU_S2),
    .pin8(AL4), .pin9(AL5), .pin10(1'b0), .pin11(AL6), .pin12(N_FLAG), .pin13(V_FLAG), .pin14(C_FLAG),
    .pin15(ALCO), .pin16(D_IN[7]), .pin17(AO7), .pin18(D_IN[6]), .pin19(AO6), .pin20(1'b1));
  _7421 _7421_1 (
    .pin1(O0), .pin2(O1), .pin4(O2), .pin5(O3), .pin6(Z_FLAG), .pin7(1'b0), .pin9(1'b0), .pin10(1'b0),
    .pin12(1'b0), .pin13(1'b0), .pin14(1'b1));  // open: pin3, pin8, pin11
  _7402 _7402_1 (
    .pin1(O0), .pin2(AL0), .pin3(AL1), .pin4(O1), .pin5(AL2), .pin6(AL3), .pin7(1'b0), .pin8(AL4),
    .pin9(AL5), .pin10(O2), .pin11(AL6), .pin12(N_FLAG), .pin13(O3), .pin14(1'b1));

  // Other names for the same wires on the sheet: AL7 = N_FLAG; ALC = C_FLAG; ALU_OE = nALU_OE; ALV = V_FLAG;
  //   ALZ = Z_FLAG; D0 = D_IN[0]; D1 = D_IN[1]; D2 = D_IN[2]; D3 = D_IN[3]; D4 = D_IN[4]; D5 = D_IN[5]; D6 = D_IN[6];
  //   D7 = D_IN[7]; DO0 = ALU[0]; DO1 = ALU[1]; DO2 = ALU[2]; DO3 = ALU[3]; DO4 = ALU[4]; DO5 = ALU[5]; DO6 = ALU[6];
  //   DO7 = ALU[7]; SHR = nSHR; SHR_D7 = SHR_IN0
endmodule
