// Digital circuit CPU.dig as structural Verilog
module CPU (
  input  CLK,
  input  clk_2,
  input  CLK_SEL,
  output [7:0] opcode,
  output [15:0] rom
);

  wire A_LD, A_OE, A_SEL, addr_dec_1_p2, addr_dec_1_p3, alu_1_c_flag, alu_1_n_flag, alu_1_v_flag,
       alu_1_z_flag, ALU_CIN, ALU_S0, ALU_S1, ALU_S2, and_1_out, and_2_out, C, CLK_t, FL_SEL, keyboard_1_av,
       MAR_DIR, MEM_RD, MEM_WR, mmio_1_kb_en, N, nALU_OE, nFL_LD, nFL_OE, nHALT, nHBA_OE, nIR_LD, nIRA_OE,
       nIRD_OE, nMAR_INC, nMAR_OE, nMARH_LD, nMARL_LD, nMMIO_CS, nMPC_RST, nPC_LD, nPCH_OE, nPCL_OE, nRST,
       nSHR, nSP_INC, nSP_LD, nSP_OE, nSPH_OE, nSPL_OE, nXY_AOE, nXY_INC, PC_INC, PC_OE, REG_LD, REG_OE, RST,
       RST_out, SHR_IN0, SP_DIR, SRC_SEL, V, XY_DIR, Z;
  wire [2:0] Rsrc;
  wire [3:0] max7219_sim_1_dig1, max7219_sim_1_dig2, max7219_sim_1_dig3, max7219_sim_1_dig4,
       max7219_sim_1_dig5, max7219_sim_1_dig6, max7219_sim_1_dig7, max7219_sim_1_dig8;
  wire [4:0] mmio_1_spi_out;
  wire [7:0] alu_1_alu, ir_1_ab, keyboard_1_d, mmio_1_display, pc_1_p11;
  wire [15:0] addr_buffer_1_a_bus;
  wire [15:8] keyboard_1_d_2;
  wire [15:9] ctrlunit_1_c32_47;

  Button #(.activeLow("true")) u_RST (.out(RST_out));
  RST_HARDWARE rst_hardware_1 (.CLK(CLK_t), .RST_IN(RST_out), .RST(RST), .nRST(nRST));
  and and_1 (and_1_out, CLK, ~CLK_SEL);  // And
  and and_2 (and_2_out, CLK_SEL, clk_2);
  or or_1 (CLK_t, and_1_out, and_2_out);
  addr_buffer addr_buffer_1 (.AB_L(ir_1_ab), .nHBA_OE(nHBA_OE), .nRST(nRST), .A_BUS(addr_buffer_1_a_bus));
  Seven_Seg_Hex seven_seg_hex_1 (.d(max7219_sim_1_dig8), .dp(1'b0));
  Seven_Seg_Hex seven_seg_hex_2 (.d(max7219_sim_1_dig7), .dp(1'b0));
  // ADDR_DEC addr_dec_1: pin names not known; wires that end beside it: addr_buffer_1_a_bus, addr_dec_1_p2, addr_dec_1_p3, nMMIO_CS
  Seven_Seg_Hex seven_seg_hex_3 (.d(max7219_sim_1_dig6), .dp(1'b0));
  // PC pc_1: pin names not known; wires that end beside it: addr_buffer_1_a_bus, PC_INC, nPC_LD, PC_OE, nPCL_OE, nPCH_OE, CLK_t, RST, nRST, addr_buffer_1_a_bus, pc_1_p11
  // SP sp_1: pin names not known; wires that end beside it: addr_buffer_1_a_bus, nSP_INC, SP_DIR, nSP_LD, nSP_OE, nSPH_OE, nSPL_OE, CLK_t
  Seven_Seg_Hex seven_seg_hex_4 (.d(max7219_sim_1_dig5), .dp(1'b0));
  // MAR mar_1: pin names not known; wires that end beside it: addr_buffer_1_a_bus, CLK_t, MAR_DIR, nMAR_INC, nMAR_OE, nMARH_LD, nMARL_LD, pc_1_p11, addr_buffer_1_a_bus, pc_1_p11
  Seven_Seg_Hex seven_seg_hex_5 (.d(max7219_sim_1_dig4), .dp(1'b0));
  RAMSinglePortSel #(.AddrBits(16), .Bits(8)) ramsingleportsel_1 (
    .A(addr_buffer_1_a_bus), .CS(~addr_dec_1_p2), .WE(MEM_WR), .OE(MEM_RD), .D(pc_1_p11));
  EEPROM #(.AddrBits(15), .Bits(16)) eeprom_1 (
    .A({1'b0, addr_buffer_1_a_bus[13:0]}), .CS(~addr_dec_1_p3), .WE(1'b0), .OE(MEM_RD), .D(rom));
  Seven_Seg_Hex seven_seg_hex_6 (.d(max7219_sim_1_dig3), .dp(1'b0));
  Seven_Seg_Hex seven_seg_hex_7 (.d(max7219_sim_1_dig2), .dp(1'b0));
  RFILE rfile_1 (
    .DB_IN(pc_1_p11), .B_10_8(opcode[2:0]), .B_7_5(Rsrc), .REG_LD_EN(REG_LD), .REG_OE_EN(REG_OE),
    .nXY_INC(nXY_INC), .XY_DIR(XY_DIR), .nXY_AOE(nXY_AOE), .SRC_SEL(SRC_SEL), .CLK(CLK_t), .RST(RST),
    .DB_OUT(pc_1_p11), .AB_OUT(addr_buffer_1_a_bus), .A_LD(A_LD), .A_OE(A_OE));
  ALU alu_1 (
    .D_IN(pc_1_p11), .A_LD(A_LD), .A_OE(A_OE), .A_SEL(A_SEL), .ALU_S0(ALU_S0), .ALU_S1(ALU_S1),
    .ALU_S2(ALU_S2), .nALU_OE(nALU_OE), .ALU_CIN(ALU_CIN), .nSHR(nSHR), .SHR_IN0(SHR_IN0), .CLK(CLK_t),
    .RST(RST), .ALU(alu_1_alu), .Z_FLAG(alu_1_z_flag), .C_FLAG(alu_1_c_flag), .N_FLAG(alu_1_n_flag),
    .V_FLAG(alu_1_v_flag), .A_R_OUT(pc_1_p11));
  IR ir_1 (
    .ROM_IN(rom), .nIRH_LD(nIR_LD), .nIRL_LD(nIRD_OE), .nIRD_OE(nIRA_OE), .nIRA_OE(CLK_t),
    ._15_11(opcode[7:3]), ._10_8(opcode[2:0]), ._7_5(Rsrc), ._0_7(pc_1_p11), .AB(ir_1_ab));  // open: CLK
  Seven_Seg_Hex seven_seg_hex_8 (.d(max7219_sim_1_dig1), .dp(1'b0));
  MMIO mmio_1 (
    .A_IN(addr_buffer_1_a_bus), .D_IN(pc_1_p11), .nMMIO_CS(nMMIO_CS), .MEM_WR(MEM_WR), .MEM_RD(MEM_RD),
    .KB_IN(keyboard_1_d), .KB_ST(keyboard_1_av), .D_OUT(pc_1_p11), .SPI_OUT(mmio_1_spi_out),
    .DISPLAY(mmio_1_display), .KB_EN(mmio_1_kb_en));
  STATUS_REG status_reg_1 (
    .D_IN(alu_1_alu), .Z_FLAG(alu_1_z_flag), .C_FLAG(alu_1_c_flag), .N_FLAG(alu_1_n_flag),
    .V_FLAG(alu_1_v_flag), .nFL_OE(nFL_OE), .nFL_LD(nFL_LD), .FL_SEL(FL_SEL), .CLK(CLK_t), .nRST(nRST),
    .D_OUT(pc_1_p11), .Z(Z), .C(C), .N(N), .V(V));
  CTRLUNIT ctrlunit_1 (
    .OPC(opcode), .Z(Z), .C(C), .N(N), .V(V), .nMPC_RST(nMPC_RST), .nHALT(nHALT), .CLK(CLK_t), .nRST(nRST),
    .C0_15({nMAR_INC, nMAR_OE, nMARH_LD, nMARL_LD, MEM_WR, MEM_RD, nMPC_RST, nHBA_OE, nIRA_OE, nIRD_OE, nIR_LD, nPCH_OE, nPCL_OE, PC_OE, nPC_LD, PC_INC}),
    .C16_31({nFL_LD, nFL_OE, SHR_IN0, nSHR, ALU_CIN, nALU_OE, ALU_S2, ALU_S1, ALU_S0, A_SEL, nXY_AOE, XY_DIR, nXY_INC, REG_OE, REG_LD, MAR_DIR}),
    .C32_47({ctrlunit_1_c32_47, nHALT, SRC_SEL, nSPH_OE, nSPL_OE, nSP_OE, nSP_LD, SP_DIR, nSP_INC, FL_SEL}));
  Keyboard keyboard_1 (.C(mmio_1_kb_en), .en(1'b1), .D({keyboard_1_d_2, keyboard_1_d}), .av(keyboard_1_av));
  LED led_1 (.in(mmio_1_display[0]));
  LED led_2 (.in(mmio_1_display[1]));
  LED led_3 (.in(mmio_1_display[2]));
  LED led_4 (.in(mmio_1_display[3]));
  LED led_5 (.in(mmio_1_display[4]));
  LED led_6 (.in(mmio_1_display[5]));
  LED led_7 (.in(mmio_1_display[6]));
  LED led_8 (.in(mmio_1_display[7]));
  max7219_sim max7219_sim_1 (
    .SCLK(mmio_1_spi_out[0]), .MOSI(mmio_1_spi_out[1]), .CS(mmio_1_spi_out[4]), .DIG1(max7219_sim_1_dig1),
    .DIG2(max7219_sim_1_dig2), .DIG3(max7219_sim_1_dig3), .DIG4(max7219_sim_1_dig4),
    .DIG5(max7219_sim_1_dig5), .DIG6(max7219_sim_1_dig6), .DIG7(max7219_sim_1_dig7), .DIG8(max7219_sim_1_dig8));

  // Other names for the same wires on the sheet: Rdst[2:0] = opcode[2:0]

  // Notes on the sheet:
  //   clk_2: Hz: 10000
  //   contents of eeprom_1 (hex, n*v repeats v):
  //   6ba,7ff,f200,e9c0,e918,6bf,701,3000,6000,d9c0,d905,700,3000,3820
  //   ,e9c0,e96f,2020,3813,0,3814,e9c0,e931,e8c0,e805,6bf,702,18,4800
  //   ,10f,0,e9c0,e973,109,ff,e9c0,e973,10a,8,e9c0,e973,10b,4,e9c0,e973
  //   ,10c,1,e9c0,e973,f900,10,3815,27,3816,e9c0,e95a,105,e9c0,e973
  //   ,e8,3815,3,3816,e9c0,e95a,104,e9c0,e973,64,3815,0,3816,e9c0,e95a
  //   ,103,e9c0,e973,a,3815,0,3816,e9c0,e95a,102,e9c0,e973,2013,101
  //   ,e9c0,e973,f900,0,3818,2013,2115,7820,3817,2014,2116,8020,d9c0
  //   ,d96d,3814,2017,3813,2018,a800,3818,e8c0,e85c,2018,f900,6bf,703
  //   ,4800,f900,3810,6bf,702,208,309,40a,50b,8,4800,820,e9c0,e985,2010
  //   ,e9c0,e985,18,4800,f900,3811,8,3812,2011,6000,3811,d8c0,d891,4840
  //   ,4860,e8c0,e893,4880,48a0,2012,b000,3812,dbc0,db88,f900
endmodule
