// Digital circuit CTRLUNIT.dig as structural Verilog
module CTRLUNIT (
  input  [7:0] OPC,
  input  Z,
  input  C,
  input  N,
  input  V,
  input  nMPC_RST,
  input  nHALT,
  input  CLK,
  input  nRST,
  output [15:0] C0_15,
  output [15:0] C16_31,
  output [15:0] C32_47
);

  wire _7408_1_pin3;
  wire [3:0] _74163_1_pin14;

  _7408 _7408_1 (
    .pin1(nRST), .pin2(nMPC_RST), .pin3(_7408_1_pin3), .pin4(1'b0), .pin5(1'b0), .pin7(1'b0), .pin9(1'b0),
    .pin10(1'b0), .pin12(1'b0), .pin13(1'b0), .pin14(1'b1));  // open: pin6, pin8, pin11
  _74163 _74163_1 (
    .pin1(_7408_1_pin3), .pin2(CLK), .pin3(1'b0), .pin4(1'b0), .pin5(1'b0), .pin6(1'b0), .pin7(nHALT),
    .pin8(1'b0), .pin9(1'b1), .pin10(nHALT), .pin11(_74163_1_pin14[3]), .pin12(_74163_1_pin14[2]),
    .pin13(_74163_1_pin14[1]), .pin14(_74163_1_pin14[0]), .pin16(1'b1));  // open: pin15
  ROM #(.AddrBits(16), .Bits(16)) _1ROM (.A({V, N, C, Z, _74163_1_pin14, OPC}), .sel(nRST), .D(C0_15));
  ROM #(.AddrBits(16), .Bits(16)) _2ROM (.A({V, N, C, Z, _74163_1_pin14, OPC}), .sel(nRST), .D(C16_31));
  ROM #(.AddrBits(16), .Bits(16)) _3ROM (.A({V, N, C, Z, _74163_1_pin14, OPC}), .sel(nRST), .D(C32_47));
  PullDown pulldown_1 (.out(C0_15[0]));
  PullUp pullup_1 (.out(C0_15[1]));
  PullDown pulldown_2 (.out(C16_31[0]));
  PullDown pulldown_3 (.out(C16_31[1]));
  PullUp pullup_2 (.out(C32_47[1]));
  PullUp pullup_3 (.out(C32_47[0]));
  PullDown pulldown_4 (.out(C0_15[2]));
  PullUp pullup_4 (.out(C0_15[3]));
  PullUp pullup_5 (.out(C0_15[4]));
  PullUp pullup_6 (.out(C0_15[5]));
  PullDown pulldown_5 (.out(C16_31[2]));
  PullUp pullup_7 (.out(C16_31[3]));
  PullUp pullup_8 (.out(C16_31[5]));
  PullUp pullup_9 (.out(C16_31[4]));
  PullDown pulldown_6 (.out(C32_47[2]));
  PullUp pullup_10 (.out(C32_47[3]));
  PullUp pullup_11 (.out(C32_47[5]));
  PullDown pulldown_7 (.out(C32_47[4]));
  PullUp pullup_12 (.out(C0_15[6]));
  PullUp pullup_13 (.out(C0_15[7]));
  PullUp pullup_14 (.out(C0_15[8]));
  PullUp pullup_15 (.out(C0_15[9]));
  PullDown pulldown_8 (.out(C16_31[7]));
  PullDown pulldown_9 (.out(C16_31[8]));
  PullDown pulldown_10 (.out(C16_31[9]));
  PullUp pullup_16 (.out(C16_31[6]));
  PullDown pulldown_11 (.out(C32_47[9]));
  PullUp pullup_17 (.out(C32_47[6]));
  PullUp pullup_18 (.out(C32_47[8]));
  PullUp pullup_19 (.out(C32_47[7]));
  PullDown pulldown_12 (.out(C0_15[12]));
  PullUp pullup_20 (.out(C0_15[10]));
  PullUp pullup_21 (.out(C0_15[11]));
  PullUp pullup_22 (.out(C0_15[13]));
  PullUp pullup_23 (.out(C16_31[11]));
  PullDown pulldown_13 (.out(C16_31[10]));
  PullDown pulldown_14 (.out(C16_31[12]));
  PullUp pullup_24 (.out(C16_31[13]));
  PullDown pulldown_15 (.out(C32_47[11]));
  PullDown pulldown_16 (.out(C32_47[12]));
  PullDown pulldown_17 (.out(C32_47[13]));
  PullUp pullup_25 (.out(C32_47[10]));
  PullDown pulldown_18 (.out(C0_15[14]));
  PullDown pulldown_19 (.out(C0_15[15]));
  PullUp pullup_26 (.out(C16_31[15]));
  PullDown pulldown_20 (.out(C16_31[14]));
  PullDown pulldown_21 (.out(C32_47[14]));
  PullDown pulldown_22 (.out(C32_47[15]));

  // Notes on the sheet:
  //   contents of _1ROM (hex, n*v repeats v):
  //   256*6f9a,8*2b7b,8*2bfb,2b7b,2b7b,2bfb,2bfb,23fb,33fb,10*2bfb,8*68ff
  //   ,8*6bff,8*4bff,8*a8ff,8*abff,8*8bff,8*abff,8*2fff,8*2bfb,8*2b7b
  //   ,32*2bfb,8*2b7b,16*2bfb,16*2b7b,24*2bfb,8*2b7b,2ffb,2f7b,2ffb
  //   ,2f7b,2ffb,2f7b,2ffb,2f7b,2bfb,bfd,2bfb,bfd,2bfb,bfd,2bfb,bfd
  //   ,2f7b,2f7b,2bfd,bfd,2ffb,2ffb,2bfb,2bfb,2bff,2ffb,bff,5*2bfb,4fbf
  //   ,2fff,2bfb,2bfb,2bfb,abff,2fff,2ffb,88*2ffa,8*6bfe,120*2ffa,2bfb
  //   ,6f9a,2bfb,6f9a,2bfb,6f9a,2bfb,6f9a,8*2ffa,6f9a,6f9a,2ffa,2ffa
  //   ,afee,afee,2ffa,2ffa,2ffa,2bfa,6*2ffa,2b7a,6ffe,4*2ffa,6bfe,217*2ffa
  //   ,8*2f7b,8*2ffa,2f7a,2f7b,2ffa,2ffa,aff6,aff6,11*2ffa,6ffe,222*2ffa
  //   ,8*2bfc,8*2ffa,2bfc,afee,2ffa,2ffa,2bfc,bfc,11*2ffa,2bfc,239*2ffa
  //   ,aff6,255*2ffa,2bfc,2326*2ffa,256*6f9a,8*2b7b,8*2bfb,2b7b,2b7b
  //   ,2bfb,2bfb,23fb,33fb,10*2bfb,8*68ff,8*6bff,8*4bff,8*a8ff,8*abff
  //   ,8*8bff,8*abff,8*2fff,8*2bfb,8*2b7b,32*2bfb,8*2b7b,16*2bfb,16*2b7b
  //   ,24*2bfb,8*2b7b,2ffb,2f7b,2f7b,2ffb,2ffb,2f7b,2ffb,2f7b,2bfb,bfd,bfd
  //   ,2bfb,2bfb,bfd,2bfb,bfd,2f7b,2f7b,2bfd,bfd,2ffb,2ffb,2bfb,2bfb
  //   ,2bff,2ffb,bff,5*2bfb,4fbf,2fff,2bfb,2bfb,2bfb,abff,2fff,2ffb
  //   ,88*2ffa,8*6bfe,120*2ffa,2bfb,6f9a,6f9a,2bfb,2bfb,6f9a,2bfb,6f9a
  //   ,8*2ffa,6f9a,6f9a,2ffa,2ffa,afee,afee,2ffa,2ffa,2ffa,2bfa,6*2ffa
  //   ,2b7a,6ffe,4*2ffa,6bfe,217*2ffa,8*2f7b,8*2ffa,2f7a,2f7b,2ffa,2ffa
  //   ,aff6,aff6,11*2ffa,6ffe,222*2ffa,8*2bfc,8*2ffa,2bfc,afee,2ffa,2ffa
  //   ,2bfc,bfc,11*2ffa,2bfc,239*2ffa,aff6,255*2ffa,2bfc,2326*2ffa,256*6f9a
  //   ,8*2b7b,8*2bfb,2b7b,2b7b,2bfb,2bfb,23fb,33fb,10*2bfb,8*68ff,8*6bff
  //   ,8*4bff,8*a8ff,8*abff,8*8bff,8*abff,8*2fff,8*2bfb,8*2b7b,32*2bfb
  //   ,8*2b7b,16*2bfb,16*2b7b,24*2bfb,8*2b7b,2f7b,2ffb,2ffb,2f7b,2ffb
  //   ,2f7b,2ffb,2f7b,bfd,2bfb,2bfb,bfd,2bfb,bfd,2bfb,bfd,2f7b,2f7b
  //   ,2bfd,bfd,2ffb,2ffb,2bfb,2bfb,2bff,2ffb,bff,5*2bfb,4fbf,2fff,2bfb,2bfb,2bfb
  //   ,abff,2fff,2ffb,88*2ffa,8*6bfe,120*2ffa,6f9a,2bfb,2bfb,6f9a,2bfb
  //   ,6f9a,2bfb,6f9a,8*2ffa,6f9a,6f9a,2ffa,2ffa,afee,afee,2ffa,2ffa,2ffa
  //   ,2bfa,6*2ffa,2b7a,6ffe,4*2ffa,6bfe,217*2ffa,8*2f7b,8*2ffa,2f7a
  //   ,2f7b,2ffa,2ffa,aff6,aff6,11*2ffa,6ffe,222*2ffa,8*2bfc,8*2ffa
  //   ,2bfc,afee,2ffa,2ffa,2bfc,bfc,11*2ffa,2bfc,239*2ffa,aff6,255*2ffa
  //   ,2bfc,2326*2ffa,256*6f9a,8*2b7b,8*2bfb,2b7b,2b7b,2bfb,2bfb,23fb
  //   ,33fb,10*2bfb,8*68ff,8*6bff,8*4bff,8*a8ff,8*abff,8*8bff,8*abff
  //   ,8*2fff,8*2bfb,8*2b7b,32*2bfb,8*2b7b,16*2bfb,16*2b7b,24*2bfb,8*2b7b
  //   ,2f7b,2ffb,2f7b,2ffb,2ffb,2f7b,2ffb,2f7b,bfd,2bfb,bfd,2bfb,2bfb
  //   ,bfd,2bfb,bfd,2f7b,2f7b,2bfd,bfd,2ffb,2ffb,2bfb,2bfb,2bff,2ffb
  //   ,bff,5*2bfb,4fbf,2fff,2bfb,2bfb,2bfb,abff,2fff,2ffb,88*2ffa,8*6bfe
  //   ,120*2ffa,6f9a,2bfb,6f9a,2bfb,2bfb,6f9a,2bfb,6f9a,8*2ffa,6f9a,6f9a
  //   ,2ffa,2ffa,afee,afee,2ffa,2ffa,2ffa,2bfa,6*2ffa,2b7a,6ffe,4*2ffa
  //   ,6bfe,217*2ffa,8*2f7b,8*2ffa,2f7a,2f7b,2ffa,2ffa,aff6,aff6,11*2ffa
  //   ,6ffe,222*2ffa,8*2bfc,8*2ffa,2bfc,afee,2ffa,2ffa,2bfc,bfc,11*2ffa
  //   ,2bfc,239*2ffa,aff6,255*2ffa,2bfc,2326*2ffa,256*6f9a,8*2b7b,8*2bfb
  //   ,2b7b,2b7b,2bfb,2bfb,23fb,33fb,10*2bfb,8*68ff,8*6bff,8*4bff,8*a8ff
  //   ,8*abff,8*8bff,8*abff,8*2fff,8*2bfb,8*2b7b,32*2bfb,8*2b7b,16*2bfb
  //   ,16*2b7b,24*2bfb,8*2b7b,2ffb,2f7b,2ffb,2f7b,2f7b,2ffb,2ffb,2f7b
  //   ,2bfb,bfd,2bfb,bfd,bfd,2bfb,2bfb,bfd,2f7b,2f7b,2bfd,bfd,2ffb,2ffb
  //   ,2bfb,2bfb,2bff,2ffb,bff,5*2bfb,4fbf,2fff,2bfb,2bfb,2bfb,abff
  //   ,2fff,2ffb,88*2ffa,8*6bfe,120*2ffa,2bfb,6f9a,2bfb,6f9a,6f9a,2bfb,2bfb
  //   ,6f9a,8*2ffa,6f9a,6f9a,2ffa,2ffa,afee,afee,2ffa,2ffa,2ffa,2bfa
  //   ,6*2ffa,2b7a,6ffe,4*2ffa,6bfe,217*2ffa,8*2f7b,8*2ffa,2f7a,2f7b
  //   ,2ffa,2ffa,aff6,aff6,11*2ffa,6ffe,222*2ffa,8*2bfc,8*2ffa,2bfc
  //   ,afee,2ffa,2ffa,2bfc,bfc,11*2ffa,2bfc,239*2ffa,aff6,255*2ffa,2bfc
  //   ,2326*2ffa,256*6f9a,8*2b7b,8*2bfb,2b7b,2b7b,2bfb,2bfb,23fb,33fb
  //   ,10*2bfb,8*68ff,8*6bff,8*4bff,8*a8ff,8*abff,8*8bff,8*abff,8*2fff
  //   ,8*2bfb,8*2b7b,32*2bfb,8*2b7b,16*2bfb,16*2b7b,24*2bfb,8*2b7b,2ffb
  //   ,2f7b,2f7b,2ffb,2f7b,2ffb,2ffb,2f7b,2bfb,bfd,bfd,2bfb,bfd,2bfb,2bfb
  //   ,bfd,2f7b,2f7b,2bfd,bfd,2ffb,2ffb,2bfb,2bfb,2bff,2ffb,bff,5*2bfb
  //   ,4fbf,2fff,2bfb,2bfb,2bfb,abff,2fff,2ffb,88*2ffa,8*6bfe,120*2ffa
  //   ,2bfb,6f9a,6f9a,2bfb,6f9a,2bfb,2bfb,6f9a,8*2ffa,6f9a,6f9a,2ffa,2ffa
  //   ,afee,afee,2ffa,2ffa,2ffa,2bfa,6*2ffa,2b7a,6ffe,4*2ffa,6bfe,217*2ffa
  //   ,8*2f7b,8*2ffa,2f7a,2f7b,2ffa,2ffa,aff6,aff6,11*2ffa,6ffe,222*2ffa
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  //   contents of _2ROM (hex, n*v repeats v):
  //   256*a878,8*a879,8*a87b,a870,a868,a838,a83c,4*a878,a872,a86a,6*a878
  //   ,8*a879,8*a859,8*a879,8*a87a,8*a85a,16*a87a,8*a878,8*abfb,8*abf9
  //   ,8*abfb,8*bafb,8*aafb,8*aefb,8*aef9,8*adfb,8*acfb,8*bbf9,8*aaf9
  //   ,16*8879,8*ba7a,8*ba78,a878,a868,a878,a868,a878,a868,a878,a868
  //   ,8*a878,a868,a868,a858,5*a878,a858,a870,4*a878,a879,a879,5*a878
  //   ,2878,90*a878,8*a879,145*a878,a868,6*a878,a879,a870,222*a878,8*a870
  //   ,8*a878,a870,a870,15*a878,a868,222*a878,8*a858,8*a878,a858,a878,a878,a878
  //   ,a858,12*a878,a858,495*a878,a858,2582*a878,8*a879,8*a87b,a870
  //   ,a868,a838,a83c,4*a878,a872,a86a,6*a878,8*a879,8*a859,8*a879,8*a87a
  //   ,8*a85a,16*a87a,8*a878,8*abfb,8*abf9,8*abfb,8*bafb,8*aafb,8*aefb
  //   ,8*aef9,8*adfb,8*acfb,8*bbf9,8*aaf9,16*8879,8*ba7a,8*ba78,a878
  //   ,a868,a868,a878,a878,a868,a878,a868,8*a878,a868,a868,a858,5*a878
  //   ,a858,a870,4*a878,a879,a879,5*a878,2878,90*a878,8*a879,145*a878
  //   ,a868,6*a878,a879,a870,222*a878,8*a870,8*a878,a870,a870,15*a878
  //   ,a868,222*a878,8*a858,8*a878,a858,a878,a878,a878,a858,12*a878
  //   ,a858,495*a878,a858,2582*a878,8*a879,8*a87b,a870,a868,a838,a83c
  //   ,4*a878,a872,a86a,6*a878,8*a879,8*a859,8*a879,8*a87a,8*a85a,16*a87a
  //   ,8*a878,8*abfb,8*abf9,8*bbfb,16*bafb,8*aefb,8*aef9,8*adfb,8*acfb
  //   ,8*bbf9,8*aaf9,8*8879,8*c879,8*ba7a,8*ba78,a868,a878,a878,a868
  //   ,a878,a868,a878,a868,8*a878,a868,a868,a858,5*a878,a858,a870,4*a878
  //   ,a879,a879,5*a878,2878,90*a878,8*a879,145*a878,a868,6*a878,a879
  //   ,a870,222*a878,8*a870,8*a878,a870,a870,15*a878,a868,222*a878,8*a858
  //   ,8*a878,a858,a878,a878,a878,a858,12*a878,a858,495*a878,a858,2582*a878
  //   ,8*a879,8*a87b,a870,a868,a838,a83c,4*a878,a872,a86a,6*a878,8*a879
  //   ,8*a859,8*a879,8*a87a,8*a85a,16*a87a,8*a878,8*abfb,8*abf9,8*bbfb
  //   ,16*bafb,8*aefb,8*aef9,8*adfb,8*acfb,8*bbf9,8*aaf9,8*8879,8*c879
  //   ,8*ba7a,8*ba78,a868,a878,a868,a878,a878,a868,a878,a868,8*a878
  //   ,a868,a868,a858,5*a878,a858,a870,4*a878,a879,a879,5*a878,2878
  //   ,90*a878,8*a879,145*a878,a868,6*a878,a879,a870,222*a878,8*a870
  //   ,8*a878,a870,a870,15*a878,a868,222*a878,8*a858,8*a878,a858,a878,a878,a878
  //   ,a858,12*a878,a858,495*a878,a858,2582*a878,8*a879,8*a87b,a870
  //   ,a868,a838,a83c,4*a878,a872,a86a,6*a878,8*a879,8*a859,8*a879,8*a87a
  //   ,8*a85a,16*a87a,8*a878,8*abfb,8*abf9,8*abfb,8*bafb,8*aafb,8*aefb
  //   ,8*aef9,8*adfb,8*acfb,8*bbf9,8*aaf9,16*8879,8*ba7a,8*ba78,a878
  //   ,a868,a878,a868,a868,a878,a878,a868,8*a878,a868,a868,a858,5*a878
  //   ,a858,a870,4*a878,a879,a879,5*a878,2878,90*a878,8*a879,145*a878
  //   ,a868,6*a878,a879,a870,222*a878,8*a870,8*a878,a870,a870,15*a878
  //   ,a868,222*a878,8*a858,8*a878,a858,a878,a878,a878,a858,12*a878
  //   ,a858,495*a878,a858,2582*a878,8*a879,8*a87b,a870,a868,a838,a83c
  //   ,4*a878,a872,a86a,6*a878,8*a879,8*a859,8*a879,8*a87a,8*a85a,16*a87a
  //   ,8*a878,8*abfb,8*abf9,8*abfb,8*bafb,8*aafb,8*aefb,8*aef9,8*adfb
  //   ,8*acfb,8*bbf9,8*aaf9,16*8879,8*ba7a,8*ba78,a878,a868,a868,a878
  //   ,a868,a878,a878,a868,8*a878,a868,a868,a858,5*a878,a858,a870,4*a878
  //   ,a879,a879,5*a878,2878,90*a878,8*a879,145*a878,a868,6*a878,a879
  //   ,a870,222*a878,8*a870,8*a878,a870,a870,15*a878,a868,222*a878,8*a858
  //   ,8*a878,a858,a878,a878,a878,a858,12*a878,a858,495*a878,a858,2582*a878
  //   ,8*a879,8*a87b,a870,a868,a838,a83c,4*a878,a872,a86a,6*a878,8*a879
  //   ,8*a859,8*a879,8*a87a,8*a85a,16*a87a,8*a878,8*abfb,8*abf9,8*bbfb
  //   ,16*bafb,8*aefb,8*aef9,8*adfb,8*acfb,8*bbf9,8*aaf9,8*8879,8*c879
  //   ,8*ba7a,8*ba78,a868,a878,a878,a868,a868,a878,a878,a868,8*a878
  //   ,a868,a868,a858,5*a878,a858,a870,4*a878,a879,a879,5*a878,2878
  //   ,90*a878,8*a879,145*a878,a868,6*a878,a879,a870,222*a878,8*a870
  //   ,8*a878,a870,a870,15*a878,a868,222*a878,8*a858,8*a878,a858,a878,a878,a878
  //   ,a858,12*a878,a858,495*a878,a858,2582*a878,8*a879,8*a87b,a870
  //   ,a868,a838,a83c,4*a878,a872,a86a,6*a878,8*a879,8*a859,8*a879,8*a87a
  //   ,8*a85a,16*a87a,8*a878,8*abfb,8*abf9,8*bbfb,16*bafb,8*aefb,8*aef9
  //   ,8*adfb,8*acfb,8*bbf9,8*aaf9,8*8879,8*c879,8*ba7a,8*ba78,a868
  //   ,a878,a868,a878,a868,a878,a878,a868,8*a878,a868,a868,a858,5*a878
  //   ,a858,a870,4*a878,a879,a879,5*a878,2878,90*a878,8*a879,145*a878
  //   ,a868,6*a878,a879,a870,222*a878,8*a870,8*a878,a870,a870,15*a878
  //   ,a868,222*a878,8*a858,8*a878,a858,a878,a878,a878,a858,12*a878
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  //   contents of _3ROM (hex, n*v repeats v):
  //   312*5eb,8*7eb,16*5eb,8*5b3,8*5a3,40*5e8,32*5ea,16*5e8,16*5eb,16*5e8
  //   ,24*5eb,5cb,56b,5cb,5e3,5f3,5eb,4eb,56b,5eb,5a3,5eb,5eb,5eb,5b3
  //   ,5a3,89*5eb,8*5ab,140*5eb,5b3,5b3,5eb,5eb,5eb,4eb,7*5eb,5a3,4*5eb
  //   ,5ac,1eb,236*5eb,5b3,5b3,11*5eb,5ab,239*5eb,5b3,255*5eb,5b3,2894*5eb
  //   ,8*7eb,16*5eb,8*5b3,8*5a3,40*5e8,32*5ea,16*5e8,16*5eb,16*5e8,24*5eb
  //   ,5cb,56b,5cb,5e3,5f3,5eb,4eb,56b,5eb,5a3,5eb,5eb,5eb,5b3,5a3,89*5eb
  //   ,8*5ab,140*5eb,5b3,5b3,5eb,5eb,5eb,4eb,7*5eb,5a3,4*5eb,5ac,1eb
  //   ,236*5eb,5b3,5b3,11*5eb,5ab,239*5eb,5b3,255*5eb,5b3,2894*5eb,8*7eb
  //   ,16*5eb,8*5b3,8*5a3,40*5e8,32*5ea,16*5e8,16*5eb,16*5e8,24*5eb
  //   ,5cb,56b,5cb,5e3,5f3,5eb,4eb,56b,5eb,5a3,5eb,5eb,5eb,5b3,5a3,89*5eb
  //   ,8*5ab,140*5eb,5b3,5b3,5eb,5eb,5eb,4eb,7*5eb,5a3,4*5eb,5ac,1eb
  //   ,236*5eb,5b3,5b3,11*5eb,5ab,239*5eb,5b3,255*5eb,5b3,2894*5eb,8*7eb
  //   ,16*5eb,8*5b3,8*5a3,40*5e8,32*5ea,16*5e8,16*5eb,16*5e8,24*5eb
  //   ,5cb,56b,5cb,5e3,5f3,5eb,4eb,56b,5eb,5a3,5eb,5eb,5eb,5b3,5a3,89*5eb
  //   ,8*5ab,140*5eb,5b3,5b3,5eb,5eb,5eb,4eb,7*5eb,5a3,4*5eb,5ac,1eb
  //   ,236*5eb,5b3,5b3,11*5eb,5ab,239*5eb,5b3,255*5eb,5b3,2894*5eb,8*7eb
  //   ,16*5eb,8*5b3,8*5a3,40*5e8,32*5ea,16*5e8,16*5eb,16*5e8,24*5eb
  //   ,5cb,56b,5cb,5e3,5f3,5eb,4eb,56b,5eb,5a3,5eb,5eb,5eb,5b3,5a3,89*5eb
  //   ,8*5ab,140*5eb,5b3,5b3,5eb,5eb,5eb,4eb,7*5eb,5a3,4*5eb,5ac,1eb
  //   ,236*5eb,5b3,5b3,11*5eb,5ab,239*5eb,5b3,255*5eb,5b3,2894*5eb,8*7eb
  //   ,16*5eb,8*5b3,8*5a3,40*5e8,32*5ea,16*5e8,16*5eb,16*5e8,24*5eb
  //   ,5cb,56b,5cb,5e3,5f3,5eb,4eb,56b,5eb,5a3,5eb,5eb,5eb,5b3,5a3,89*5eb
  //   ,8*5ab,140*5eb,5b3,5b3,5eb,5eb,5eb,4eb,7*5eb,5a3,4*5eb,5ac,1eb
  //   ,236*5eb,5b3,5b3,11*5eb,5ab,239*5eb,5b3,255*5eb,5b3,2894*5eb,8*7eb
  //   ,16*5eb,8*5b3,8*5a3,40*5e8,32*5ea,16*5e8,16*5eb,16*5e8,24*5eb
  //   ,5cb,56b,5cb,5e3,5f3,5eb,4eb,56b,5eb,5a3,5eb,5eb,5eb,5b3,5a3,89*5eb
  //   ,8*5ab,140*5eb,5b3,5b3,5eb,5eb,5eb,4eb,7*5eb,5a3,4*5eb,5ac,1eb
  //   ,236*5eb,5b3,5b3,11*5eb,5ab,239*5eb,5b3,255*5eb,5b3,2894*5eb,8*7eb
  //   ,16*5eb,8*5b3,8*5a3,40*5e8,32*5ea,16*5e8,16*5eb,16*5e8,24*5eb
  //   ,5cb,56b,5cb,5e3,5f3,5eb,4eb,56b,5eb,5a3,5eb,5eb,5eb,5b3,5a3,89*5eb
  //   ,8*5ab,140*5eb,5b3,5b3,5eb,5eb,5eb,4eb,7*5eb,5a3,4*5eb,5ac,1eb
  //   ,236*5eb,5b3,5b3,11*5eb,5ab,239*5eb,5b3,255*5eb,5b3,2894*5eb,8*7eb
  //   ,16*5eb,8*5b3,8*5a3,40*5e8,32*5ea,16*5e8,16*5eb,16*5e8,24*5eb
  //   ,5cb,56b,5cb,5e3,5f3,5eb,4eb,56b,5eb,5a3,5eb,5eb,5eb,5b3,5a3,89*5eb
  //   ,8*5ab,140*5eb,5b3,5b3,5eb,5eb,5eb,4eb,7*5eb,5a3,4*5eb,5ac,1eb
  //   ,236*5eb,5b3,5b3,11*5eb,5ab,239*5eb,5b3,255*5eb,5b3,2894*5eb,8*7eb
  //   ,16*5eb,8*5b3,8*5a3,40*5e8,32*5ea,16*5e8,16*5eb,16*5e8,24*5eb
  //   ,5cb,56b,5cb,5e3,5f3,5eb,4eb,56b,5eb,5a3,5eb,5eb,5eb,5b3,5a3,89*5eb
  //   ,8*5ab,140*5eb,5b3,5b3,5eb,5eb,5eb,4eb,7*5eb,5a3,4*5eb,5ac,1eb
  //   ,236*5eb,5b3,5b3,11*5eb,5ab,239*5eb,5b3,255*5eb,5b3,2894*5eb,8*7eb
  //   ,16*5eb,8*5b3,8*5a3,40*5e8,32*5ea,16*5e8,16*5eb,16*5e8,24*5eb
  //   ,5cb,56b,5cb,5e3,5f3,5eb,4eb,56b,5eb,5a3,5eb,5eb,5eb,5b3,5a3,89*5eb
  //   ,8*5ab,140*5eb,5b3,5b3,5eb,5eb,5eb,4eb,7*5eb,5a3,4*5eb,5ac,1eb
  //   ,236*5eb,5b3,5b3,11*5eb,5ab,239*5eb,5b3,255*5eb,5b3,2894*5eb,8*7eb
  //   ,16*5eb,8*5b3,8*5a3,40*5e8,32*5ea,16*5e8,16*5eb,16*5e8,24*5eb
  //   ,5cb,56b,5cb,5e3,5f3,5eb,4eb,56b,5eb,5a3,5eb,5eb,5eb,5b3,5a3,89*5eb
  //   ,8*5ab,140*5eb,5b3,5b3,5eb,5eb,5eb,4eb,7*5eb,5a3,4*5eb,5ac,1eb
  //   ,236*5eb,5b3,5b3,11*5eb,5ab,239*5eb,5b3,255*5eb,5b3,2894*5eb,8*7eb
  //   ,16*5eb,8*5b3,8*5a3,40*5e8,32*5ea,16*5e8,16*5eb,16*5e8,24*5eb
  //   ,5cb,56b,5cb,5e3,5f3,5eb,4eb,56b,5eb,5a3,5eb,5eb,5eb,5b3,5a3,89*5eb
  //   ,8*5ab,140*5eb,5b3,5b3,5eb,5eb,5eb,4eb,7*5eb,5a3,4*5eb,5ac,1eb
  //   ,236*5eb,5b3,5b3,11*5eb,5ab,239*5eb,5b3,255*5eb,5b3,2894*5eb,8*7eb
  //   ,16*5eb,8*5b3,8*5a3,40*5e8,32*5ea,16*5e8,16*5eb,16*5e8,24*5eb
  //   ,5cb,56b,5cb,5e3,5f3,5eb,4eb,56b,5eb,5a3,5eb,5eb,5eb,5b3,5a3,89*5eb
  //   ,8*5ab,140*5eb,5b3,5b3,5eb,5eb,5eb,4eb,7*5eb,5a3,4*5eb,5ac,1eb
  //   ,236*5eb,5b3,5b3,11*5eb,5ab,239*5eb,5b3,255*5eb,5b3,2894*5eb,8*7eb
  //   ,16*5eb,8*5b3,8*5a3,40*5e8,32*5ea,16*5e8,16*5eb,16*5e8,24*5eb
  //   ,5cb,56b,5cb,5e3,5f3,5eb,4eb,56b,5eb,5a3,5eb,5eb,5eb,5b3,5a3,89*5eb
  //   ,8*5ab,140*5eb,5b3,5b3,5eb,5eb,5eb,4eb,7*5eb,5a3,4*5eb,5ac,1eb
  //   ,236*5eb,5b3,5b3,11*5eb,5ab,239*5eb,5b3,255*5eb,5b3,2894*5eb,8*7eb
  //   ,16*5eb,8*5b3,8*5a3,40*5e8,32*5ea,16*5e8,16*5eb,16*5e8,24*5eb
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endmodule
